// Digital circuit 2_demultiplexor_de_1_entrada_4_salidas.dig as structural Verilog
module _2_demultiplexor_de_1_entrada_4_salidas (
  input  x0,
  input  x1,
  input  Input,
  output Output0,
  output Output1,
  output Output2,
  output Output3
);

  wire not_1_out, not_2_out;

  not not_1 (not_1_out, x1);
  not not_2 (not_2_out, x0);
  and and_1 (Output0, Input, not_1_out, not_2_out);
  and and_2 (Output1, Input, not_1_out, x0);
  and and_3 (Output2, Input, x1, not_2_out);
  and and_4 (Output3, Input, x1, x0);
endmodule
