// Digital circuit 3_flip_flop_rs_y_jk.dig as structural Verilog
module _3_flip_flop_rs_y_jk (
  input  Set,
  input  Reset,
  input  J,
  input  K,
  input  Clock2,
  input  Clock1,
  output Q,
  output Q_2,
  output Q_3,
  output Q_4
);

  wire nand_1_out, nand_2_out, nand_3_out, nand_4_out, nand_5_out, nand_6_out, nand_7_out, nand_8_out,
       nand_9_out, nand_10_out, nand_11_out, nand_12_out, not_1_out, not_2_out;

  not not_1 (not_1_out, Clock1);
  not not_2 (not_2_out, Clock2);
  nand nand_1 (nand_1_out, Set, not_1_out);
  nand nand_2 (nand_2_out, not_1_out, Reset);
  nand nand_3 (nand_3_out, Q_4, J, not_2_out);
  nand nand_4 (nand_4_out, not_2_out, K, Q_3);
  nand nand_5 (nand_5_out, nand_1_out, nand_6_out);
  nand nand_6 (nand_6_out, nand_5_out, nand_2_out);
  nand nand_7 (nand_7_out, nand_3_out, nand_8_out);
  nand nand_8 (nand_8_out, nand_7_out, nand_4_out);
  nand nand_9 (nand_9_out, nand_5_out, Clock1);
  nand nand_10 (nand_10_out, Clock1, nand_6_out);
  nand nand_11 (nand_11_out, nand_7_out, Clock2);
  nand nand_12 (nand_12_out, Clock2, nand_8_out);
  nand nand_13 (Q, nand_9_out, Q_2);
  nand nand_14 (Q_2, Q, nand_10_out);
  nand nand_15 (Q_3, nand_11_out, Q_4);
  nand nand_16 (Q_4, Q_3, nand_12_out);

  // Notes on the sheet:
  //   Flip Flop RS
  //   El Flip Flop RS está compuesto por varias compuertas NAND que se retroalimenta entre sí, con el fin de cambiar a la vez los estados de Q y Q´, 
  //   adicionalmente existen otras compuertas lógicas NAND dentro del circuito que cumplen la función de Enable, la cual está sujeto a un reloj.
  //   Cuando se establece un valor de 1 por las entradas R y S, el circuito empieza a oscilar, debido a la retroalimentación de las compuertas NAND. 
  //   Cuando el valor es opuesto para las entradas R y S, la salida Q adopta el valor de S y Q´ el valor de R cuando se presenta una subida por parte del reloj. 
  //   Por ejemplo el valor por la entrada S es 1  por ende el valor a la salida Q será 1, mientras que por la salida Q´ será 0 ya que por la entrada R es 0. 
  //   Por último cuando se establece un valor de 0 por las entradas R y S, el valor de de Q y Q´ no se verá alterado, con ello se guarda el estado de las salidas Q y Q´.
  //   Flip Flop JK
  //   El Flip Flop JK es similar al RS, tanto en su estructura como en su tabla de verdad (Donde J hace las veces de S y K las de R), con la diferencia de que no 
  //   se presentan oscilaciones del circuito cuando las entradas J y K toman el valor de 1, dando como resultado que las salidas Q y Q´ tomen valores intermitentes
  //    con cada ciclo del reloj.
endmodule
