// Digital circuit 1_multiplexor_de_8_entradas_1_salida.dig as structural Verilog
module _1_multiplexor_de_8_entradas_1_salida (
  input  D0,
  input  D1,
  input  D2,
  input  D3,
  input  D4,
  input  D5,
  input  D6,
  input  D7,
  input  x2,
  input  x1,
  input  x0,
  output \output 
);

  wire and_1_out, and_2_out, and_3_out, and_4_out, and_5_out, and_6_out, and_7_out, and_8_out, not_1_out,
       not_2_out, not_3_out, or_1_out, or_2_out;

  not not_1 (not_1_out, x2);
  not not_2 (not_2_out, x1);
  not not_3 (not_3_out, x0);
  and and_1 (and_1_out, D0, not_1_out, not_2_out, not_3_out);
  and and_2 (and_2_out, D1, not_1_out, not_2_out, x0);
  and and_3 (and_3_out, D2, not_1_out, x1, not_3_out);
  and and_4 (and_4_out, D3, not_1_out, x1, x0);
  and and_5 (and_5_out, D4, x2, not_2_out, not_3_out);
  and and_6 (and_6_out, D5, x2, not_2_out, x0);
  and and_7 (and_7_out, D6, x2, x1, not_3_out);
  and and_8 (and_8_out, D7, x2, x1, x0);
  or or_1 (or_1_out, and_1_out, and_2_out, and_3_out, and_4_out);
  or or_2 (or_2_out, and_5_out, and_6_out, and_7_out, and_8_out);
  or or_3 (\output , or_1_out, or_2_out);
endmodule
