// Digital circuit 4_pinIO.dig as structural Verilog
module _4_pinIO (
  input  EnableCon1,
  input  Sel1,
  input  Set,
  input  Clear,
  input  Clock,
  input  PinIn1,
  input  EnableCon2,
  input  Sel2,
  input  PinIn2,
  input  EnableCon3,
  input  Sel3,
  input  PinIn3,
  input  EnableCon4,
  input  Sel4,
  input  PinIn4,
  input  EnableCont1,
  input  Control1,
  input  EnableCont2,
  input  Control2,
  input  EnableCont3,
  input  Control3,
  input  EnableCont4,
  input  Control4,
  input  EnableAlm1,
  input  EnableAlm2,
  input  EnableAlm3,
  input  EnableAlm4,
  output Pinout1,
  output Pinout2,
  output Pinout3,
  output Pinout4,
  output AlmBit1,
  output AlmBit2,
  output AlmBit3,
  output AlmBit4
);

  wire d_ff_as_3_q, d_ff_as_6_q, d_ff_as_9_q, d_ff_as_12_q, In1, In2, In3, In4, multiplexer_1_out,
       multiplexer_2_out, multiplexer_3_out, multiplexer_4_out, multiplexer_5_out, multiplexer_6_out,
       multiplexer_7_out, multiplexer_8_out, multiplexer_9_out, multiplexer_10_out, multiplexer_11_out,
       multiplexer_12_out, Out1, Out2, Out3, Out4;

  Multiplexer multiplexer_1 (.sel(EnableAlm1), .in_0(AlmBit1), .in_1(In1), .out(multiplexer_1_out));
  Multiplexer multiplexer_2 (.sel(EnableCont1), .in_0(Out1), .in_1(Control1), .out(multiplexer_2_out));
  Multiplexer multiplexer_3 (.sel(EnableCon1), .in_0(d_ff_as_3_q), .in_1(Sel1), .out(multiplexer_3_out));
  D_FF_AS d_ff_as_1 (.Set(Set), .D(multiplexer_1_out), .C(Clock), .Clr(Clear), .Q(AlmBit1));  // open: nQ
  D_FF_AS d_ff_as_2 (.Set(Set), .D(multiplexer_2_out), .C(Clock), .Clr(Clear), .Q(Out1));  // open: nQ
  D_FF_AS d_ff_as_3 (.Set(Set), .D(multiplexer_3_out), .C(Clock), .Clr(Clear), .Q(d_ff_as_3_q));  // open: nQ
  assign In1 = d_ff_as_3_q ? PinIn1 : 1'bz;  // Driver driver_1
  assign Pinout1 = ~d_ff_as_3_q ? Out1 : 1'bz;  // DriverInvSel driverinvsel_1
  Multiplexer multiplexer_4 (.sel(EnableAlm2), .in_0(AlmBit2), .in_1(In2), .out(multiplexer_4_out));
  Multiplexer multiplexer_5 (.sel(EnableCont2), .in_0(Out2), .in_1(Control2), .out(multiplexer_5_out));
  Multiplexer multiplexer_6 (.sel(EnableCon2), .in_0(d_ff_as_6_q), .in_1(Sel2), .out(multiplexer_6_out));
  D_FF_AS d_ff_as_4 (.Set(Set), .D(multiplexer_4_out), .C(Clock), .Clr(Clear), .Q(AlmBit2));  // open: nQ
  D_FF_AS d_ff_as_5 (.Set(Set), .D(multiplexer_5_out), .C(Clock), .Clr(Clear), .Q(Out2));  // open: nQ
  D_FF_AS d_ff_as_6 (.Set(Set), .D(multiplexer_6_out), .C(Clock), .Clr(Clear), .Q(d_ff_as_6_q));  // open: nQ
  assign In2 = d_ff_as_6_q ? PinIn2 : 1'bz;  // Driver driver_2
  assign Pinout2 = ~d_ff_as_6_q ? Out2 : 1'bz;  // DriverInvSel driverinvsel_2
  Multiplexer multiplexer_7 (.sel(EnableAlm3), .in_0(AlmBit3), .in_1(In3), .out(multiplexer_7_out));
  Multiplexer multiplexer_8 (.sel(EnableCont3), .in_0(Out3), .in_1(Control3), .out(multiplexer_8_out));
  Multiplexer multiplexer_9 (.sel(EnableCon3), .in_0(d_ff_as_9_q), .in_1(Sel3), .out(multiplexer_9_out));
  D_FF_AS d_ff_as_7 (.Set(Set), .D(multiplexer_7_out), .C(Clock), .Clr(Clear), .Q(AlmBit3));  // open: nQ
  D_FF_AS d_ff_as_8 (.Set(Set), .D(multiplexer_8_out), .C(Clock), .Clr(Clear), .Q(Out3));  // open: nQ
  D_FF_AS d_ff_as_9 (.Set(Set), .D(multiplexer_9_out), .C(Clock), .Clr(Clear), .Q(d_ff_as_9_q));  // open: nQ
  assign In3 = d_ff_as_9_q ? PinIn3 : 1'bz;  // Driver driver_3
  assign Pinout3 = ~d_ff_as_9_q ? Out3 : 1'bz;  // DriverInvSel driverinvsel_3
  Multiplexer multiplexer_10 (.sel(EnableAlm4), .in_0(AlmBit4), .in_1(In4), .out(multiplexer_10_out));
  Multiplexer multiplexer_11 (.sel(EnableCont4), .in_0(Out4), .in_1(Control4), .out(multiplexer_11_out));
  Multiplexer multiplexer_12 (.sel(EnableCon4), .in_0(d_ff_as_12_q), .in_1(Sel4), .out(multiplexer_12_out));
  D_FF_AS d_ff_as_10 (.Set(Set), .D(multiplexer_10_out), .C(Clock), .Clr(Clear), .Q(AlmBit4));  // open: nQ
  D_FF_AS d_ff_as_11 (.Set(Set), .D(multiplexer_11_out), .C(Clock), .Clr(Clear), .Q(Out4));  // open: nQ
  D_FF_AS d_ff_as_12 (.Set(Set), .D(multiplexer_12_out), .C(Clock), .Clr(Clear), .Q(d_ff_as_12_q));  // open: nQ
  assign In4 = d_ff_as_12_q ? PinIn4 : 1'bz;  // Driver driver_4
  assign Pinout4 = ~d_ff_as_12_q ? Out4 : 1'bz;  // DriverInvSel driverinvsel_4

  // Notes on the sheet:
  //   Registros de 
  //   Almacenamiento
  //   Registros de 
  //   Control
  //   Registros de 
  //   Configuracion
  //   PIN I/O 1
  //   PIN I/O 2
  //   PIN I/O 3
  //   PIN I/O 4
endmodule
